// Logisim project isa_8_bits.circ as structural Verilog: 3 circuits, main circuit main
module main (
);

  wire BRZR, CLK, DADO_BREG, MUX_ULA, REG_A, W_BREG, WM;
  wire [1:0] multiplexer_3_out, PC_SEL;
  wire [2:0] OP_ULA;
  wire [3:0] OPCODE, rom_1_data;
  wire [7:0] adder_1_out, IMM, multiplexer_1_out, multiplexer_2_out, multiplexer_4_out, multiplexer_5_out,
       PC_IMM, PC_q, RA, ram_1_dout, RB, ula_1_c;

  Clock clock_1 (.out(CLK));
  Multiplexer #(.width(8)) multiplexer_1 (.in0(adder_1_out), .in1(RB), .out(multiplexer_1_out), .sel(BRZR));
  Multiplexer #(.select(2), .width(8)) multiplexer_2 (
    .in0(adder_1_out), .in1(PC_IMM), .in2(multiplexer_1_out), .out(multiplexer_2_out), .sel(PC_SEL));  // open: in3
  Register PC (.D(multiplexer_2_out), .en(1'b1), .clk(CLK), .Q(PC_q));  // open: clr
  Adder adder_1 (.a(PC_q), .b(8'h1), .out(adder_1_out));  // open: cin, cout
  ROM rom_1 (.addr(PC_q), .data({OPCODE, rom_1_data}));
  Adder adder_2 (.a(PC_q), .b(IMM), .out(PC_IMM));  // open: cin, cout
  ROM #(.addrWidth(4), .dataWidth(10)) rom_2 (
    .addr(OPCODE), .data({PC_SEL, REG_A, W_BREG, MUX_ULA, DADO_BREG, WM, OP_ULA}));
  assign IMM = {{4{rom_1_data[3]}}, rom_1_data};  // Bit_Extender bit_extender_1
  Comparator comparator_1 (.a(RA), .b({8{1'b0}}), .eq(BRZR));  // open: gt, lt
  Multiplexer #(.width(2)) multiplexer_3 (.in0(rom_1_data[3:2]), .in1(2'b00), .out(multiplexer_3_out), .sel(REG_A));
  BANCO_REGISTRADORES banco_registradores_1 (
    .DADO(multiplexer_4_out), .RS1(multiplexer_3_out), .YES_NO(W_BREG), .RD(multiplexer_3_out),
    .RS2(rom_1_data[1:0]), .CLK(CLK), .A(RA), .B(RB));
  Multiplexer #(.width(8)) multiplexer_4 (.in0(ula_1_c), .in1(ram_1_dout), .out(multiplexer_4_out), .sel(DADO_BREG));
  Multiplexer #(.width(8)) multiplexer_5 (.in0(RB), .in1(IMM), .out(multiplexer_5_out), .sel(MUX_ULA));
  ULA ula_1 (.A(RA), .B(multiplexer_5_out), .OPULA(OP_ULA), .C(ula_1_c));  // open: ZERO
  RAM ram_1 (.addr(RB), .we(WM), .oe(1'b1), .clk(CLK), .din(RA), .dout(ram_1_dout));

  // Notes on the sheet:
  //   CONTROLA QUAL TIPO DE SOMA DE PC EH FEITA
  //   SE BRZR FOR 0 (RA != 0) USA PC+1, CASO CONTRARIO PC+RB
  //   FAZ ATUALIZAÇÃO PC+1
  //   FAZ PC + IMM
  //   contents of rom_2 (hex, n*v repeats v):
  //   200 100 50 8 e4 0 0 0 40 41 42 43 44 45 46 47
  //   ESCREVE NO BANCO
  //   UNIDADE DE CONTROLE
  //   RB
  //   RA
  //   OPCODE
  //   IMM
  //   VALIDA SE USA R[A] OU 0
  //   PARA ACEITAR SALTOS COM NUM NEGATIVOS (COMPLEMENTO DE 2)
  //   INSTRUÇÃO BRANCH ON ZERO
  //   CONTROLA SE ULA RECEBE R[B] OU IMM
  //   CONTROLA QUAL O DADO QUE VAI SER ENTRADA DA PORTA DE ESCRITA DO BREG SE USA OU MEM
  //   OPCODE DA ULA
  //   REGISTRADOR B EH O QUE INTERESSA PARA LOAD E STORE
  //   constante 1 ali serve para dizer que ali na saida temos o que recebemos como entrada
  //   O QUE VAI SER ESCRITO EM MEMORIA EH O QUE ESTA NO RA
  //   CONTROLA SE ESCREVE OU NÃO NA MEMÓRIA
endmodule

module BANCO_REGISTRADORES (
  input  [7:0] DADO,
  input  [1:0] RS1,
  input  YES_NO,
  input  [1:0] RD,
  input  [1:0] RS2,
  input  CLK,
  output [7:0] A,
  output [7:0] B
);

  wire demultiplexer_1_out0, demultiplexer_1_out1, demultiplexer_1_out2, demultiplexer_1_out3;
  wire [7:0] multiplexer_1_out, multiplexer_2_out, multiplexer_3_out, multiplexer_4_out, R0_q, R1_q, R2_q,
       R3_q;

  Demultiplexer #(.select(2)) demultiplexer_1 (
    .out0(demultiplexer_1_out0), .out1(demultiplexer_1_out1), .out2(demultiplexer_1_out2),
    .out3(demultiplexer_1_out3), .in(YES_NO), .sel(RD));
  Multiplexer #(.width(8)) multiplexer_1 (.in0(R0_q), .in1(DADO), .out(multiplexer_1_out), .sel(demultiplexer_1_out0));
  Multiplexer #(.width(8)) multiplexer_2 (.in0(R1_q), .in1(DADO), .out(multiplexer_2_out), .sel(demultiplexer_1_out1));
  Multiplexer #(.width(8)) multiplexer_3 (.in0(R2_q), .in1(DADO), .out(multiplexer_3_out), .sel(demultiplexer_1_out2));
  Multiplexer #(.width(8)) multiplexer_4 (.in0(R3_q), .in1(DADO), .out(multiplexer_4_out), .sel(demultiplexer_1_out3));
  Register R0 (.D(multiplexer_1_out), .clk(CLK), .Q(R0_q));  // open: en, clr
  Register R1 (.D(multiplexer_2_out), .clk(CLK), .Q(R1_q));  // open: en, clr
  Register R2 (.D(multiplexer_3_out), .clk(CLK), .Q(R2_q));  // open: en, clr
  Register R3 (.D(multiplexer_4_out), .clk(CLK), .Q(R3_q));  // open: en, clr
  Multiplexer #(.select(2), .width(8)) multiplexer_5 (
    .in0(R0_q), .in1(R1_q), .in2(R2_q), .in3(R3_q), .out(A), .sel(RS1));
  Multiplexer #(.select(2), .width(8)) multiplexer_6 (
    .in0(R0_q), .in1(R1_q), .in2(R2_q), .in3(R3_q), .out(B), .sel(RS2));
endmodule

module ULA (
  input  [7:0] A,
  input  [7:0] B,
  input  [2:0] OPULA,
  output ZERO,
  output [7:0] C
);

  wire [7:0] adder_1_out, and_1_out, not_1_out, or_1_out, shifter_1_out, shifter_2_out, subtractor_1_out,
       xor_1_out;

  assign not_1_out = ~B;  // NOT_Gate not_1, 8 bits wide
  assign and_1_out = A & B;  // AND_Gate and_1, 8 bits wide
  assign or_1_out = A | B;  // OR_Gate or_1, 8 bits wide
  assign xor_1_out = A ^ B;  // XOR_Gate xor_1, 8 bits wide
  Adder adder_1 (.a(A), .b(B), .out(adder_1_out));  // open: cin, cout
  Subtractor subtractor_1 (.a(A), .b(B), .out(subtractor_1_out));  // open: bin, bout
  Shifter shifter_1 (.in(A), .\dist (B[2:0]), .out(shifter_1_out));
  Shifter #(.shift("lr")) shifter_2 (.in(A), .\dist (B[2:0]), .out(shifter_2_out));
  Multiplexer #(.select(3), .width(8)) multiplexer_1 (
    .in0(not_1_out), .in1(and_1_out), .in2(or_1_out), .in3(xor_1_out), .in4(adder_1_out),
    .in5(subtractor_1_out), .in6(shifter_1_out), .in7(shifter_2_out), .out(C), .sel(OPULA));
  Comparator comparator_1 (.a({8{1'b0}}), .b(C), .eq(ZERO));  // open: gt, lt

  // Notes on the sheet:
  //   NOT
  //   AND
  //   OR
  //   XOR
  //   SOMADOR
  //   SUBTRATOR
  //   SHIFT_LEFT
  //   SHIFT_LEFT
endmodule
